# Fritzing sketch LF-HF-RFID-Detector (saved by Fritzing 0.9.3b)
circuit board: 8.56cm x 5.39801cm
breadboards: 1

parts:
  C1 = Capacitor [package=0805]
  C2 = Capacitor [package=0805]
  C3 = Capacitor [package=0805]
  C4 = Capacitor [package=0805]
  C5 = Capacitor [package=0805]
  LED1 = smd LED [color="Red (633nm)" package="0603 [SMD]"]
  C7 = Capacitor [package=0805]
  C8 = Capacitor [package=0805]
  C9 = Capacitor [package=0805]
  C6 = Capacitor [package=0805]
  LED2 = smd LED [color="Red (633nm)" package="0603 [SMD]"]

nets:
  N1: C1.1, C3.1, C4.1, C5.1, LED1.cathode
  N2: C1.2, C2.1
  N3: C2.2, C3.2, C4.2, C5.2, LED1.anode
  N4: C7.1, C8.1, C9.1, C6.1, LED2.cathode
  N5: C7.2, C8.2, C9.2, C6.2, LED2.anode

notes:
  HF
  LF
  LF/HF RFID Field Detector
  by Corey Harding
  Founder of: https://www.LegacySecurityGroup.com
  Rev 0.01
  125kHz
  13.56MHz
  LF/HF RFID
  Field Detector
